# Fritzing sketch pratica1 (saved by Fritzing 0.9.2b)

parts:
  Part1 = Intel Galileo Gen2
  LED1 = smd LED [color="Red (633nm)" package="1206 [SMD]"]

nets:
  N1: Part1.D13/SCK, LED1.anode
  N2: Part1.GND, LED1.cathode
