# Fritzing sketch Pratica2 (saved by Fritzing 0.9.2b)
breadboards: 1

parts:
  LED1 = smd LED [color="Red (633nm)" package="1206 [SMD]"]
  Part1 = Intel Galileo Gen2
  R2 = PHOTOCELL [package=photocell-kit]
  R3 = Rotary Potentiometer (Large) [maximum_resistance=100kΩ package=THT]

nets:
  N1: LED1.cathode, Part1.GND, R2.P$1
  N2: LED1.anode, Part1.D13/SCK
  N3: Part1.A0, R2.P$2, R3.wiper
  N4: Part1.5V, R3.leg2

// code stored in the sketch: pratica2Arduino.ino
#define pinoLed 13 // Pino no qual o LED estah conectado
int leituraAD = 0;// leitura do sensor LDR a ser feita com o conversor AD por meio da funcao analogRead().
                  // conversao  5 V -> 1023  (10 bits) 11111 11111
                  //            0 V - > 0              00000 00000
float sensorLuz;// Valor analogico aproximado da leitura do sensor

void setup()
{

Serial.begin(9600);//inicia a comunicacao serial Galileo -> Computador 
                   //                                    <-
pinMode(pinoLed, OUTPUT);// seleciona a porta digital pinoLed para saida 

}


char letra = 'a';
char * texto = "isso eh um texto";
void loop()
{
leituraAD = analogRead(A0);// ler o sinal anal?gico na porta digital A0

sensorLuz = (float) ( leituraAD * 5)/1023; //regra de 3 escala de 0 a 1023 digital, para 0 a 5 anal?gico

Serial.print("Leitura AD = ");
Serial.print(leituraAD);

Serial.print(" Conversao para float  = ");
Serial.println(sensorLuz);


delay(500); // faz nada por 500 ms

}
