# Fritzing sketch Pratica3 (saved by Fritzing 0.9.2b)
breadboards: 1

parts:
  LED1 = smd LED [color="Red (633nm)" package="1206 [SMD]"]
  Part1 = Intel Galileo Gen2
  S7 = Pushbutton [package="[THT]"]
  R1 = Resistor [tolerance=±5% resistance=10k package="0805 [SMD]"]
  R2 = Resistor [tolerance=±5% resistance=220 package=THT]
  LED2 = smd LED [color="Yellow (595nm)" package="1206 [SMD]"]
  LED3 = smd LED [color="Green (565nm)" package="1206 [SMD]"]
  LED4 = smd LED [color="Blue (505nm)" package="1206 [SMD]"]
  R3 = Resistor [tolerance=±5% resistance=220 package=THT]
  R4 = Resistor [tolerance=±5% resistance=220 package=THT]
  R5 = Resistor [tolerance=±5% resistance=220 package=THT]

nets:
  N1: LED1.cathode, Part1.GND, R1.Pin_0, LED4.cathode
  N2: LED1.anode, R2.Pin_1
  N3: Part1.D2, S7.Pin_1, S7.Pin_2, R1.Pin_1
  N4: Part1.D3_PWM, R2.Pin_0
  N5: Part1.D4, R3.Pin_0
  N6: Part1.D5_PWM, R4.Pin_0
  N7: Part1.D6_PWM, R5.Pin_0
  N8: Part1.5V, S7.Pin_3, S7.Pin_4
  N9: LED2.anode, R3.Pin_1
  N10: LED3.anode, R4.Pin_1
  N11: LED4.anode, R5.Pin_1

// code stored in the sketch: pratica3code.ino
#define pinoBotao 2
#define pinoLedVermelho 3
#define pinoLedAmarelo 4
#define pinoLedVerde 5
#define pinoLedAzul 6
#define tempoDelay 300

void setup()
{
	pinMode(pinoBotao, INPUT); // Define o pino 2 como input de tensao
	pinMode(pinoLedVermelho, OUTPUT); // Define o pino 3 como output de tensao
	pinMode(pinoLedAmarelo, OUTPUT); // Define o pino 4 como output de tensao
	pinMode(pinoLedVerde, OUTPUT); // Define o pino 5 como output de tensao
	pinMode(pinoLedAzul, OUTPUT); // Define o pino 6 como output de tensao

}

int cont = 1;

void loop()
{
   
    if(digitalRead(pinoBotao) == HIGH)
    {
	     cont = cont + 1;

			 if(cont > 6)
			 {
					cont = 1;
			 }	
    }
	  
    if(cont == 1)
		{
		  digitalWrite(pinoLedVermelho, HIGH);
      digitalWrite(pinoLedAmarelo, HIGH);
			digitalWrite(pinoLedVerde, HIGH);
			digitalWrite(pinoLedAzul, HIGH);
      
			delay(tempoDelay);
			
			digitalWrite(pinoLedVermelho, LOW);
      digitalWrite(pinoLedAmarelo, LOW);
			digitalWrite(pinoLedVerde, LOW);
			digitalWrite(pinoLedAzul, LOW);
      
			delay(tempoDelay);
			
		}
		else
		{
			digitalWrite(cont, HIGH);
						
			delay(tempoDelay);
						
			digitalWrite(cont, LOW);
						
			delay(tempoDelay);
		}
}
