# Fritzing sketch pratica4 (saved by Fritzing 0.9.2b)
breadboards: 1

parts:
  Part2 = Intel Galileo Gen2
  R6 = Resistor [tolerance=±5% resistance=220 package=THT]
  R7 = Resistor [tolerance=±5% resistance=220 package=THT]
  R8 = Resistor [tolerance=±5% resistance=220 package=THT]
  R9 = Resistor [tolerance=±5% resistance=220 package=THT]
  LED5 = smd LED [color="Blue (505nm)" package="1206 [SMD]"]
  LED6 = smd LED [color="Green (565nm)" package="1206 [SMD]"]
  LED7 = smd LED [color="Yellow (595nm)" package="1206 [SMD]"]
  LED8 = smd LED [color="Red (633nm)" package="1206 [SMD]"]
  S8 = Pushbutton [package="[THT]"]
  R10 = Resistor [tolerance=±5% resistance=10k package="0805 [SMD]"]

nets:
  N1: Part2.D2, S8.Pin_1, S8.Pin_2, R10.Pin_1
  N2: Part2.D3_PWM, R9.Pin_0
  N3: Part2.D4, R8.Pin_0
  N4: Part2.D5_PWM, R7.Pin_0
  N5: Part2.D6_PWM, R6.Pin_0
  N6: Part2.5V, S8.Pin_3, S8.Pin_4
  N7: Part2.GND, LED8.cathode, R10.Pin_0
  N8: R6.Pin_1, LED5.anode
  N9: R7.Pin_1, LED6.anode
  N10: R8.Pin_1, LED7.anode
  N11: R9.Pin_1, LED8.anode
