# Fritzing sketch pratica42 (saved by Fritzing 0.9.2b)
breadboards: 1

parts:
  Part2 = Intel Galileo Gen2
  R6 = Resistor [tolerance=±5% resistance=220 package=THT]
  R7 = Resistor [tolerance=±5% resistance=220 package=THT]
  R8 = Resistor [tolerance=±5% resistance=220 package=THT]
  R9 = Resistor [tolerance=±5% resistance=220 package=THT]
  LED5 = smd LED [color="Blue (505nm)" package="1206 [SMD]"]
  LED6 = smd LED [color="Green (565nm)" package="1206 [SMD]"]
  LED7 = smd LED [color="Yellow (595nm)" package="1206 [SMD]"]
  LED8 = smd LED [color="Red (633nm)" package="1206 [SMD]"]
  S8 = Pushbutton [package="[THT]"]
  R10 = Resistor [tolerance=±5% resistance=10k package="0805 [SMD]"]
  R11 = Rotary Potentiometer (Large) [maximum_resistance=100kΩ package=THT]

nets:
  N1: Part2.A0, R11.wiper
  N2: Part2.D2, S8.Pin_1, S8.Pin_2, R10.Pin_1
  N3: Part2.D3_PWM, R9.Pin_0
  N4: Part2.D4, R8.Pin_0
  N5: Part2.D5_PWM, R7.Pin_0
  N6: Part2.D6_PWM, R6.Pin_0
  N7: Part2.5V, S8.Pin_3, S8.Pin_4, R11.leg2
  N8: Part2.GND, LED8.cathode, R10.Pin_0, R11.leg1
  N9: R6.Pin_1, LED5.anode
  N10: R7.Pin_1, LED6.anode
  N11: R8.Pin_1, LED7.anode
  N12: R9.Pin_1, LED8.anode

// code stored in the sketch: pratica4code.ino
#define pinoBotao 2
#define tempoDelayPadrao 200
#define ledAzul 3
#define ledverde 4
#define ledAmarelo 5
#define ledvermelho 6

void setup()
{ 
	int i;
  for( i = 3; i <= 6; i++)//usando o laco for para definir as portas 3 a 6 como portas de saida
	{
			pinMode(i, OUTPUT); // Define o pino 3 como output de tensao
	}
   
	pinMode(pinoBotao, INPUT); // Define o pino 2 como input de tensao

}

int comportamento = 0;
int i;
int sensorA0;
void loop()
{
		i = 0;

		for( i = ledAzul ; i <= ledVermelho; i++) //Apagando todos LEDs
				{
						digitalWrite(i, LOW);
				}
		i= 0;

    sensorA0 = analogRead(A0);// 0 < sensorA0 <= 1023

		if(digitalRead(pinoBotao) == HIGH)//Altera o comportamento a ser obedecido ao aperta o botao
		{
				comportamento += 1;
				if(comportamento > 3)
				comportamento = 0;
		}

	  switch (comportamento)
		{
	
			case 1:// Comportamento 1: Piscar apenas um LED a depender do valor de tensao lido no potenciometro
				if(sensorA0 < 250)
				{
						while( i < 7)
						{
								if( i == ledAzul)
								{
										digitalWrite(i, LOW);
										delay(sensorA0);
										digitalWrite(i, HIGH);
										delay(sensorA0);
								}
								else
								{
										digitalWrite(i, LOW);
										
								}
							i++;
						}
						i = 0;
				}
				else if(sensorA0 >= 250 && sensor < 500)
				{
						while( i < 7)
						{
								if( i == ledVerde)
								{
										digitalWrite(i, LOW);
										delay(sensorA0);
										digitalWrite(i, HIGH);
										delay(sensorA0);
								}
								else
								{
										digitalWrite(i, LOW);
										
								}
							i++;
						}
						i = 0;
				}
				else if(sensor >= 500 && sensor < 750)
				{
						while( i < 7)
						{
								if( i == ledAmarelo)
								{
										digitalWrite(i, LOW);
										delay(sensorA0);
										digitalWrite(i, HIGH);
										delay(sensorA0);
								}
								else
								{
										digitalWrite(i, LOW);
										
								}
							i++;
						}
						i = 0;
				}
				else if(sensor >= 750 && sensor <= 1023)
				{
						while( i < 7)
						{
								if( i == ledVermelho)
								{
										digitalWrite(i, LOW);
										delay(sensorA0);
										digitalWrite(i, HIGH);
										delay(sensorA0);
								}
								else
								{
										digitalWrite(i, LOW);
										
								}
							i++;
						}
						
						i = 0;
				}
			break;

			case 2://Comportamento 2: piscar os leds, do azul ao vermelho com velocidade determinada pelo potenciometro
				for( i = ledAzul ; i <= ledVermelho; i++)
				{
						
										digitalWrite(i, HIGH);
										delay(sensorA0);
										digitalWrite(i, LOW);
										delay(sensorA0);
				}

			break;
			case 3://Comportamento 3: COMPORTAMENTO A SER ESCOLHIDO PELOS ALUNOS
				for( i = ledVermelho ; i >= ledAzul; i--)// NESSE EXEMPLO, FOI ESCOLHIDO REALIZAR O COMPORTAMENTO INVERSOR AO COMPORTAMENTO 2
				{
						
										digitalWrite(i, HIGH);
										delay(sensorA0);
										digitalWrite(i, LOW);
										delay(sensorA0);
				}
			break;
			default:
				for( i = ledAzul ; i <= ledVermelho; i++)
				{
						
										digitalWrite(i, LOW);
				}
		}

}
