# Fritzing sketch pratica5 (saved by Fritzing 0.9.2b)
breadboards: 1

parts:
  Part1 = Intel Galileo
  U1 = 74HC595 [package="DIP16 [THT]"]
  R1 = Resistor [tolerance=±5% resistance=220 package="0603 [SMD]"]
  R2 = Resistor [tolerance=±5% resistance=220 package="0603 [SMD]"]
  R3 = Resistor [tolerance=±5% resistance=220 package="0603 [SMD]"]
  R4 = Resistor [tolerance=±5% resistance=220 package="0603 [SMD]"]
  R5 = Resistor [tolerance=±5% resistance=220 package="0603 [SMD]"]
  R6 = Resistor [tolerance=±5% resistance=220 package="0603 [SMD]"]
  R7 = Resistor [tolerance=±5% resistance=220 package="0603 [SMD]"]
  R8 = Resistor [tolerance=±5% resistance=220 package="0603 [SMD]"]
  LED1 = smd LED [color="Red (633nm)" package="0805 [SMD]"]
  LED2 = smd LED [color="Red (633nm)" package="0805 [SMD]"]
  LED3 = smd LED [color="Red (633nm)" package="0805 [SMD]"]
  LED4 = smd LED [color="Red (633nm)" package="0805 [SMD]"]
  LED5 = smd LED [color="Red (633nm)" package="0805 [SMD]"]
  LED6 = smd LED [color="Red (633nm)" package="0805 [SMD]"]
  LED7 = smd LED [color="Red (633nm)" package="0805 [SMD]"]
  LED8 = smd LED [color="Red (633nm)" package="0805 [SMD]"]

nets:
  GND: Part1.GND, U1.GND, U1.OE, LED1.cathode, LED2.cathode, LED3.cathode, LED4.cathode, LED5.cathode, LED6.cathode, LED7.cathode, LED8.cathode
  N1: Part1.D5_PWM, U1.DS
  N2: Part1.D6_PWM, U1.ST_CP
  N3: Part1.D7, U1.SH_CP
  5V: Part1.5V, U1.MR, U1.VCC
  N4: U1.Q1, R2.Pin_0
  N5: U1.Q2, R3.Pin_0
  N6: U1.Q3, R4.Pin_0
  N7: U1.Q4, R5.Pin_0
  N8: U1.Q5, R6.Pin_0
  N9: U1.Q6, R7.Pin_0
  N10: U1.Q7, R8.Pin_0
  N11: U1.Q0, R1.Pin_0
  N12: R1.Pin_1, LED1.anode
  N13: R2.Pin_1, LED2.anode
  N14: R3.Pin_1, LED3.anode
  N15: R4.Pin_1, LED4.anode
  N16: R5.Pin_1, LED5.anode
  N17: R6.Pin_1, LED6.anode
  N18: R7.Pin_1, LED7.anode
  N19: R8.Pin_1, LED8.anode

// code stored in the sketch: pratica5code.ino

#define pinoClock  7
#define pinoLatch  6
#define pinoData  5

byte numeroOut = 0;// byte = 8 bits
int bits[8];
int i;
void setup() {
pinMode(pinoLatch, OUTPUT);
pinMode(pinoClock, OUTPUT);
pinMode(pinoData, OUTPUT);
Serial.begin(9600);

//Setando a variavel bits = B11100101
bits[0] = 1; bits[1] = 0;bits[2] = 1;bits[3] = 0;bits[4] = 0;bits[5] = 1;bits[6] = 1;bits[7] = 1;

//calculando o numero a ser usado na função shiftOut usando a regra mostrada na seção 4.3.13
	for(i = 0; i < 8; i++)
	{
		numeroOut += bits[i]*pow(2,i);
	}

}

void loop() {


digitalWrite(pinoLatch, LOW);

// envia dados nos pinos de saida a partir do bit menos significa
//tivo da variavel numeroOut no pinoData

shiftOut(pinoData, pinoClock, LSBFIRST, numeroOut); 
// utilizar shiftOut(pinoData, pinoClock, LSBFIRST, B11100101); 
// funcionaria da mesma forma, visto que o compilador sabe lidar com as bases decimal, binária, octal e hexadecimal
// Entretanto, o objetico da prática e a utlização de vetores, daí forçar o cálculo binario -> decimal 


digitalWrite(pinoLatch, HIGH);
}

// code stored in the sketch: pratica5code2.ino

#define pinoClock  7
#define pinoLatch  6
#define pinoData  5

int i,j, temp;
int digitosResto[8];
void setup() {
pinMode(pinoLatch, OUTPUT);
pinMode(pinoClock, OUTPUT);
pinMode(pinoData, OUTPUT);
Serial.begin(9600);


}

void loop() 
{

	for(i = 0 ; i <= 255; i++)
	{
		digitalWrite(pinoLatch, LOW);
	
// envia dados nos pinos de saida a partir do bit menos significa
//tivo da variavel numeroOut no pinoData

		shiftOut(pinoData, pinoClock, LSBFIRST, i);
		Serial.print("Contagem = ");
    Serial.print(i);

		temp = i;// tem eh a variavel temporaria que passara pelo processo de divisoes sucessivas a cada iteracao
    j = 7; //indice dos resto inicial (digito menos significativo)
		Serial.print(" = ");
		while(j != 0)
		{   
				digitosResto[j] = temp%2;//registra o resto
				j--;
				temp /= 2;//atualizar o dividendo
				
		}
		
		//Imprimindo o numero na base binaria na ordem correta
		for(j = 0; j < 8; j++)
		{
				Serial.print(digitosResto[j]);
		}
		
		Serial.println();


		digitalWrite(pinoLatch, HIGH);
		delay(500);	
	}
}
