# Fritzing sketch pratica6 (saved by Fritzing 0.9.2b)
breadboards: 1

parts:
  T1 = LM35 Temperature Sensor [package="TO92 [THT]"]
  Part1 = Intel Galileo
  LED1 = LED - 3mm [color="Blue (505nm)" package="3 mm [THT]"]
  LED2 = LED - 3mm [color="Green (565nm)" package="3 mm [THT]"]
  LED3 = LED - 3mm [color="Red (633nm)" package="3 mm [THT]"]
  R1 = Resistor [tolerance=±5% resistance=220 package=THT]
  R2 = Resistor [tolerance=±5% resistance=220 package=THT]
  R3 = Resistor [tolerance=±5% resistance=220 package=THT]

nets:
  N1: T1.+Vs, Part1.5V
  N2: T1.Vout, Part1.A0
  GND: T1.GND, Part1.GND, R1.Pin_1, R2.Pin_1, R3.Pin_1
  N3: Part1.D2, LED3.anode
  N4: Part1.D3_PWM, LED2.anode
  N5: Part1.D4, LED1.anode
  N6: LED1.cathode, R1.Pin_0
  N7: LED2.cathode, R2.Pin_0
  N8: LED3.cathode, R3.Pin_0

// code stored in the sketch: pratica6code.ino
#define ledQuente 2
#define ledNormal 3
#define ledFrio 4	
#define temperaturaAmbiente 24.0
//funcao para inicializar as portas digitasis
void inicializaPortasDigitais()
{
 		pinMode(ledQuente, OUTPUT);
  		pinMode(ledNormal, OUTPUT);
		pinMode(ledFrio, OUTPUT);
}
//funcao para inicilizar a comunicacao serial de forma a poder printar a temperatura no monitor serial
void inicializaSerial()
{
	Serial.begin(9600);
}

// funcao para ler a pora analogica porta e converter o valor lido para float
float leTemperatura(int porta)
{
	float valorLido;
    int sensor;
	
	sensor = analogRead(porta);
	valorLido = (float)(sensor*5)/1023; // regra de tres entre as escalas 0 -> 1023  ; 0 -> 5
	// aqui valorLido guarda o valor da tensão lida nos terminais do LM35

	valorLido = valorLido/0.01; // Agora, valorLido guardar a temperatura lida (sensibilidade LM35 = 10mV/C) 

	return valorLido;
}

void escreveTemperaturaTerminal(float temperatura)
{
	Serial.print("Temperatura = ");
	Serial.print(temperatura);
}

void piscaLed(float temperatura)
{		
		if(temperatura > temperaturaAmbiente  - 2 &&  temperatura < temperaturaAmbiente +2 )
		{
				digitalWrite(ledQuente, LOW);
				digitalWrite(ledFrio, LOW);
				digitalWrite(ledNormal, HIGH);
		}
		else if ( temperatura >= temperaturaAmbiente +2 )
		{
				digitalWrite(ledQuente, HIGH);
				digitalWrite(ledFrio, LOW);
				digitalWrite(ledNormal, LOW);
		}
		else if( temperatura <= temperaturaAmbiente - 2)
		{
				digitalWrite(ledQuente, LOW);
				digitalWrite(ledFrio, HIGH);
				digitalWrite(ledNormal, LOW);
		}

}


void setup()
{
	inicalizaPortasDigitais();
    inicialzaSerial();
}

float temperatura;
void loop()
{
	temperatura = leTemperatura(0);
	escreveTemperaturaTerminal(temperatura);
	piscaLed(temperatura);
	
	delay(300);
}
